// Logisim project Converter.circ as structural Verilog: 10 circuits, main circuit 4bits to 8bits
module _4bits_to_8bits (
  input  [3:0] in_1,
  output [7:0] out_2
);

  Hex_Digit_Display hex_digit_display_1 ();  // open: value, dp
  Hex_Digit_Display hex_digit_display_2 ();  // open: value, dp

  assign out_2 = {4'b0000, in_1};
endmodule

module _8bits_to_16bits (
  input  [7:0] in_1,
  output [15:0] out_2
);


  assign out_2 = {{8{1'b0}}, in_1};
endmodule

module _16bits_to_32bits (
  input  [15:0] in_1,
  output [31:0] out_2
);


  assign out_2 = {{16{1'b0}}, in_1};
endmodule

module Digits_to_Binary (
  input  [3:0] in_1,
  input  [3:0] in_2,
  input  [3:0] in_3,
  input  [3:0] in_4,
  input  [3:0] in_5,
  output [15:0] out_6
);

  wire [7:0] n4bits_to_8bits_1_out_2, n4bits_to_8bits_2_out_2, n4bits_to_8bits_3_out_2,
       n4bits_to_8bits_4_out_2, n4bits_to_8bits_5_out_2;
  wire [15:0] adder_1_out, adder_2_out, adder_3_out, multiplier_1_out, multiplier_2_out, multiplier_3_out,
       multiplier_4_out, n8bits_to_16bits_1_out_2, n8bits_to_16bits_2_out_2, n8bits_to_16bits_3_out_2,
       n8bits_to_16bits_4_out_2, n8bits_to_16bits_5_out_2;

  _8bits_to_16bits u_8bits_to_16bits_1 (.in_1(n4bits_to_8bits_1_out_2), .out_2(n8bits_to_16bits_1_out_2));
  _4bits_to_8bits u_4bits_to_8bits_1 (.in_1(in_1), .out_2(n4bits_to_8bits_1_out_2));
  _8bits_to_16bits u_8bits_to_16bits_2 (.in_1(n4bits_to_8bits_2_out_2), .out_2(n8bits_to_16bits_2_out_2));
  _4bits_to_8bits u_4bits_to_8bits_2 (.in_1(in_2), .out_2(n4bits_to_8bits_2_out_2));
  _4bits_to_8bits u_4bits_to_8bits_3 (.in_1(in_3), .out_2(n4bits_to_8bits_3_out_2));
  _8bits_to_16bits u_8bits_to_16bits_3 (.in_1(n4bits_to_8bits_3_out_2), .out_2(n8bits_to_16bits_3_out_2));
  _8bits_to_16bits u_8bits_to_16bits_4 (.in_1(n4bits_to_8bits_4_out_2), .out_2(n8bits_to_16bits_4_out_2));
  _4bits_to_8bits u_4bits_to_8bits_4 (.in_1(in_4), .out_2(n4bits_to_8bits_4_out_2));
  Multiplier #(.width(16)) multiplier_1 (
    .a(n8bits_to_16bits_1_out_2), .b(16'h2710), .out(multiplier_1_out));  // open: cin, cout
  Multiplier #(.width(16)) multiplier_2 (
    .a(n8bits_to_16bits_2_out_2), .b(16'h3e8), .out(multiplier_2_out));  // open: cin, cout
  Multiplier #(.width(16)) multiplier_3 (
    .a(n8bits_to_16bits_3_out_2), .b(16'h64), .out(multiplier_3_out));  // open: cin, cout
  Multiplier #(.width(16)) multiplier_4 (
    .a(n8bits_to_16bits_4_out_2), .b(16'ha), .out(multiplier_4_out));  // open: cin, cout
  _8bits_to_16bits u_8bits_to_16bits_5 (.in_1(n4bits_to_8bits_5_out_2), .out_2(n8bits_to_16bits_5_out_2));
  _4bits_to_8bits u_4bits_to_8bits_5 (.in_1(in_5), .out_2(n4bits_to_8bits_5_out_2));
  Adder #(.width(16)) adder_1 (.a(multiplier_1_out), .b(multiplier_2_out), .out(adder_1_out));  // open: cin, cout
  Adder #(.width(16)) adder_2 (.a(adder_1_out), .b(multiplier_3_out), .out(adder_2_out));  // open: cin, cout
  Adder #(.width(16)) adder_3 (.a(adder_2_out), .b(multiplier_4_out), .out(adder_3_out));  // open: cin, cout
  Adder #(.width(16)) adder_4 (.a(adder_3_out), .b(n8bits_to_16bits_5_out_2), .out(out_6));  // open: cin, cout
endmodule

module Binary_to_Digits (
  input  [15:0] in_1,
  output [3:0] out_2,
  output [3:0] out_3,
  output [3:0] out_4,
  output [3:0] out_5,
  output [3:0] out_6
);

  wire [7:0] n16bits_to_8bits_1_out_2, n16bits_to_8bits_2_out_2, n16bits_to_8bits_3_out_2,
       n16bits_to_8bits_4_out_2, n16bits_to_8bits_5_out_2;
  wire [15:0] divider_1_out, divider_2_out, divider_3_out, divider_4_out, multiplier_1_out, multiplier_2_out,
       multiplier_3_out, multiplier_4_out, subtractor_1_out, subtractor_2_out, subtractor_3_out,
       subtractor_4_out;

  Divider #(.width(16)) divider_1 (.a(in_1), .b(16'h2710), .out(divider_1_out));  // open: upper, rem
  Subtractor #(.width(16)) subtractor_1 (.a(in_1), .b(multiplier_1_out), .out(subtractor_1_out));  // open: bin, bout
  Divider #(.width(16)) divider_2 (.a(subtractor_1_out), .b(16'h3e8), .out(divider_2_out));  // open: upper, rem
  Subtractor #(.width(16)) subtractor_2 (
    .a(subtractor_1_out), .b(multiplier_2_out), .out(subtractor_2_out));  // open: bin, bout
  Divider #(.width(16)) divider_3 (.a(subtractor_2_out), .b(16'h64), .out(divider_3_out));  // open: upper, rem
  Subtractor #(.width(16)) subtractor_3 (
    .a(subtractor_2_out), .b(multiplier_3_out), .out(subtractor_3_out));  // open: bin, bout
  Divider #(.width(16)) divider_4 (.a(subtractor_3_out), .b(16'ha), .out(divider_4_out));  // open: upper, rem
  Subtractor #(.width(16)) subtractor_4 (
    .a(subtractor_3_out), .b(multiplier_4_out), .out(subtractor_4_out));  // open: bin, bout
  Multiplier #(.width(16)) multiplier_1 (.a(divider_1_out), .b(16'h2710), .out(multiplier_1_out));  // open: cin, cout
  Multiplier #(.width(16)) multiplier_2 (.a(divider_2_out), .b(16'h3e8), .out(multiplier_2_out));  // open: cin, cout
  Multiplier #(.width(16)) multiplier_3 (.a(divider_3_out), .b(16'h64), .out(multiplier_3_out));  // open: cin, cout
  Multiplier #(.width(16)) multiplier_4 (.a(divider_4_out), .b(16'ha), .out(multiplier_4_out));  // open: cin, cout
  _8bits_to_4bits u_8bits_to_4bits_1 (.out_2(out_2), .in_1(n16bits_to_8bits_1_out_2));
  _16bits_to_8bits u_16bits_to_8bits_1 (.out_2(n16bits_to_8bits_1_out_2), .in_1(divider_1_out));
  _8bits_to_4bits u_8bits_to_4bits_2 (.out_2(out_3), .in_1(n16bits_to_8bits_2_out_2));
  _16bits_to_8bits u_16bits_to_8bits_2 (.out_2(n16bits_to_8bits_2_out_2), .in_1(divider_2_out));
  _16bits_to_8bits u_16bits_to_8bits_3 (.out_2(n16bits_to_8bits_3_out_2), .in_1(divider_3_out));
  _16bits_to_8bits u_16bits_to_8bits_4 (.out_2(n16bits_to_8bits_4_out_2), .in_1(divider_4_out));
  _16bits_to_8bits u_16bits_to_8bits_5 (.out_2(n16bits_to_8bits_5_out_2), .in_1(subtractor_4_out));
  _8bits_to_4bits u_8bits_to_4bits_3 (.out_2(out_4), .in_1(n16bits_to_8bits_3_out_2));
  _8bits_to_4bits u_8bits_to_4bits_4 (.out_2(out_5), .in_1(n16bits_to_8bits_4_out_2));
  _8bits_to_4bits u_8bits_to_4bits_5 (.out_2(out_6), .in_1(n16bits_to_8bits_5_out_2));
endmodule

module _16bits_to_8bits (
  input  [15:0] in_1,
  output [7:0] out_2
);


  assign out_2 = in_1[7:0];
  // also tied to GND on the sheet: {in_1[8], in_1[9], in_1[10], in_1[11], in_1[12], in_1[13], in_1[14], in_1[15]}
endmodule

module _8bits_to_4bits (
  input  [7:0] in_1,
  output [3:0] out_2
);


  assign out_2 = in_1[3:0];
  // also tied to GND on the sheet: {in_1[4], in_1[5], in_1[6], in_1[7]}
endmodule

module _16bit_Display (
  input  [15:0] in_1,
  output [3:0] out_2,
  output [3:0] out_3,
  output [3:0] out_4,
  output [3:0] out_5,
  output [3:0] out_6
);

  wire [7:0] n16bits_to_8bits_1_out_2, n16bits_to_8bits_2_out_2, n16bits_to_8bits_3_out_2,
       n16bits_to_8bits_4_out_2, n16bits_to_8bits_5_out_2;
  wire [15:0] divider_1_out, divider_2_out, divider_3_out, divider_4_out, multiplier_1_out, multiplier_2_out,
       multiplier_3_out, multiplier_4_out, subtractor_1_out, subtractor_2_out, subtractor_3_out,
       subtractor_4_out;

  Divider #(.width(16)) divider_1 (.a(in_1), .b(16'h2710), .out(divider_1_out));  // open: upper, rem
  Subtractor #(.width(16)) subtractor_1 (.a(in_1), .b(multiplier_1_out), .out(subtractor_1_out));  // open: bin, bout
  Divider #(.width(16)) divider_2 (.a(subtractor_1_out), .b(16'h3e8), .out(divider_2_out));  // open: upper, rem
  Subtractor #(.width(16)) subtractor_2 (
    .a(subtractor_1_out), .b(multiplier_2_out), .out(subtractor_2_out));  // open: bin, bout
  Divider #(.width(16)) divider_3 (.a(subtractor_2_out), .b(16'h64), .out(divider_3_out));  // open: upper, rem
  Subtractor #(.width(16)) subtractor_3 (
    .a(subtractor_2_out), .b(multiplier_3_out), .out(subtractor_3_out));  // open: bin, bout
  Divider #(.width(16)) divider_4 (.a(subtractor_3_out), .b(16'ha), .out(divider_4_out));  // open: upper, rem
  Subtractor #(.width(16)) subtractor_4 (
    .a(subtractor_3_out), .b(multiplier_4_out), .out(subtractor_4_out));  // open: bin, bout
  Multiplier #(.width(16)) multiplier_1 (.a(divider_1_out), .b(16'h2710), .out(multiplier_1_out));  // open: cin, cout
  Multiplier #(.width(16)) multiplier_2 (.a(divider_2_out), .b(16'h3e8), .out(multiplier_2_out));  // open: cin, cout
  Multiplier #(.width(16)) multiplier_3 (.a(divider_3_out), .b(16'h64), .out(multiplier_3_out));  // open: cin, cout
  Multiplier #(.width(16)) multiplier_4 (.a(divider_4_out), .b(16'ha), .out(multiplier_4_out));  // open: cin, cout
  _8bits_to_4bits u_8bits_to_4bits_1 (.out_2(out_2), .in_1(n16bits_to_8bits_1_out_2));
  _16bits_to_8bits u_16bits_to_8bits_1 (.out_2(n16bits_to_8bits_1_out_2), .in_1(divider_1_out));
  _8bits_to_4bits u_8bits_to_4bits_2 (.out_2(out_3), .in_1(n16bits_to_8bits_2_out_2));
  _16bits_to_8bits u_16bits_to_8bits_2 (.out_2(n16bits_to_8bits_2_out_2), .in_1(divider_2_out));
  _16bits_to_8bits u_16bits_to_8bits_3 (.out_2(n16bits_to_8bits_3_out_2), .in_1(divider_3_out));
  _16bits_to_8bits u_16bits_to_8bits_4 (.out_2(n16bits_to_8bits_4_out_2), .in_1(divider_4_out));
  _16bits_to_8bits u_16bits_to_8bits_5 (.out_2(n16bits_to_8bits_5_out_2), .in_1(subtractor_4_out));
  _8bits_to_4bits u_8bits_to_4bits_3 (.out_2(out_4), .in_1(n16bits_to_8bits_3_out_2));
  _8bits_to_4bits u_8bits_to_4bits_4 (.out_2(out_5), .in_1(n16bits_to_8bits_4_out_2));
  _8bits_to_4bits u_8bits_to_4bits_5 (.out_2(out_6), .in_1(n16bits_to_8bits_5_out_2));
endmodule

module Keyboard (
  input  a,
  input  b,
  input  in_3,
  input  c,
  input  d,
  input  e,
  input  f,
  input  g,
  input  h,
  input  x2,
  input  x3,
  output [15:0] out_12
);

  wire and_1_out, and_2_out, and_3_out, and_4_out, and_5_out, and_6_out, and_7_out, and_8_out, and_9_out,
       and_10_out, and_11_out, and_12_out, and_13_out, and_14_out, and_15_out, not_1_out, not_2_out,
       not_3_out, not_4_out, not_5_out, not_6_out, not_7_out, not_8_out, not_9_out, not_10_out, not_11_out,
       not_12_out, not_13_out, not_14_out, not_15_out, not_16_out, not_17_out, not_18_out, not_19_out,
       not_20_out, not_21_out, not_22_out, not_23_out, not_24_out, not_25_out, not_26_out, not_27_out,
       not_28_out, not_29_out, not_30_out, not_31_out, not_32_out, not_33_out, not_34_out, not_35_out,
       not_36_out, not_37_out, not_38_out, not_39_out, not_40_out, not_41_out, not_42_out, not_43_out,
       not_44_out, not_45_out, not_46_out, not_47_out, not_48_out, not_49_out, not_50_out, not_51_out,
       not_52_out, not_53_out, not_54_out, not_55_out, not_56_out, not_57_out, not_58_out, not_59_out,
       not_60_out, not_61_out, not_62_out, not_63_out, not_64_out, not_65_out, not_66_out, not_67_out,
       not_68_out, not_69_out, not_70_out, not_71_out, not_72_out, not_73_out, not_74_out, not_75_out,
       not_76_out, not_77_out, not_78_out, not_79_out, not_80_out, not_81_out, not_82_out, not_83_out,
       not_84_out, not_85_out, not_86_out, not_87_out, not_88_out, not_89_out, or_1_out;
  wire [3:0] or_5_out, shift_register_1_q0, shift_register_1_q1, shift_register_1_q2, shift_register_1_q3,
       shift_register_1_q4;

  or or_1 (or_1_out, a, b, c, d, e, f, g, h, x2, x3);
  not not_1 (not_1_out, c);
  not not_2 (not_2_out, d);
  not not_3 (not_3_out, e);
  not not_4 (not_4_out, f);
  not not_5 (not_5_out, g);
  not not_6 (not_6_out, h);
  not not_7 (not_7_out, x2);
  not not_8 (not_8_out, x3);
  not not_9 (not_9_out, c);
  not not_10 (not_10_out, d);
  not not_11 (not_11_out, e);
  not not_12 (not_12_out, f);
  not not_13 (not_13_out, g);
  not not_14 (not_14_out, h);
  not not_15 (not_15_out, x2);
  not not_16 (not_16_out, x3);
  not not_17 (not_17_out, a);
  not not_18 (not_18_out, b);
  not not_19 (not_19_out, g);
  not not_20 (not_20_out, h);
  not not_21 (not_21_out, x2);
  not not_22 (not_22_out, x3);
  not not_23 (not_23_out, a);
  not not_24 (not_24_out, b);
  not not_25 (not_25_out, g);
  not not_26 (not_26_out, h);
  not not_27 (not_27_out, x2);
  not not_28 (not_28_out, x3);
  not not_29 (not_29_out, a);
  not not_30 (not_30_out, b);
  not not_31 (not_31_out, g);
  not not_32 (not_32_out, h);
  not not_33 (not_33_out, x2);
  not not_34 (not_34_out, x3);
  not not_35 (not_35_out, a);
  not not_36 (not_36_out, b);
  not not_37 (not_37_out, g);
  not not_38 (not_38_out, h);
  not not_39 (not_39_out, x2);
  not not_40 (not_40_out, x3);
  not not_41 (not_41_out, a);
  not not_42 (not_42_out, b);
  not not_43 (not_43_out, e);
  not not_44 (not_44_out, f);
  not not_45 (not_45_out, x2);
  not not_46 (not_46_out, x3);
  not not_47 (not_47_out, a);
  not not_48 (not_48_out, b);
  not not_49 (not_49_out, e);
  not not_50 (not_50_out, f);
  not not_51 (not_51_out, x2);
  not not_52 (not_52_out, x3);
  not not_53 (not_53_out, a);
  not not_54 (not_54_out, b);
  not not_55 (not_55_out, e);
  not not_56 (not_56_out, f);
  not not_57 (not_57_out, x2);
  not not_58 (not_58_out, x3);
  not not_59 (not_59_out, a);
  not not_60 (not_60_out, b);
  not not_61 (not_61_out, e);
  not not_62 (not_62_out, f);
  not not_63 (not_63_out, x2);
  not not_64 (not_64_out, x3);
  not not_65 (not_65_out, b);
  not not_66 (not_66_out, d);
  not not_67 (not_67_out, f);
  not not_68 (not_68_out, h);
  not not_69 (not_69_out, x3);
  not not_70 (not_70_out, b);
  not not_71 (not_71_out, d);
  not not_72 (not_72_out, f);
  not not_73 (not_73_out, h);
  not not_74 (not_74_out, x3);
  not not_75 (not_75_out, b);
  not not_76 (not_76_out, d);
  not not_77 (not_77_out, f);
  not not_78 (not_78_out, h);
  not not_79 (not_79_out, x3);
  not not_80 (not_80_out, b);
  not not_81 (not_81_out, d);
  not not_82 (not_82_out, f);
  not not_83 (not_83_out, h);
  not not_84 (not_84_out, x3);
  not not_85 (not_85_out, b);
  not not_86 (not_86_out, d);
  not not_87 (not_87_out, f);
  not not_88 (not_88_out, h);
  not not_89 (not_89_out, x3);
  and and_1 (and_1_out, b, not_1_out, not_2_out, not_3_out, not_4_out, not_5_out, not_6_out, not_7_out, not_8_out);
  and and_2 (and_2_out, a, not_9_out, not_10_out, not_11_out, not_12_out, not_13_out, not_14_out, not_15_out, not_16_out);
  and and_3 (and_3_out, not_17_out, not_18_out, f, not_19_out, not_20_out, not_21_out, not_22_out);
  and and_4 (and_4_out, not_23_out, not_24_out, e, not_25_out, not_26_out, not_27_out, not_28_out);
  and and_5 (and_5_out, not_29_out, not_30_out, d, not_31_out, not_32_out, not_33_out, not_34_out);
  and and_6 (and_6_out, not_35_out, not_36_out, c, not_37_out, not_38_out, not_39_out, not_40_out);
  and and_7 (and_7_out, not_41_out, not_42_out, not_43_out, not_44_out, h, not_45_out, not_46_out);
  and and_8 (and_8_out, not_47_out, not_48_out, not_49_out, not_50_out, g, not_51_out, not_52_out);
  and and_9 (and_9_out, not_53_out, not_54_out, d, not_55_out, not_56_out, not_57_out, not_58_out);
  and and_10 (and_10_out, not_59_out, not_60_out, c, not_61_out, not_62_out, not_63_out, not_64_out);
  and and_11 (and_11_out, not_65_out, not_66_out, not_67_out, not_68_out, x2, not_69_out);
  and and_12 (and_12_out, not_70_out, not_71_out, not_72_out, g, not_73_out, not_74_out);
  and and_13 (and_13_out, not_75_out, not_76_out, e, not_77_out, not_78_out, not_79_out);
  and and_14 (and_14_out, not_80_out, c, not_81_out, not_82_out, not_83_out, not_84_out);
  and and_15 (and_15_out, a, not_85_out, not_86_out, not_87_out, not_88_out, not_89_out);
  or or_2 (or_5_out[3], and_1_out, and_2_out);
  or or_3 (or_5_out[2], and_3_out, and_4_out, and_5_out, and_6_out);
  or or_4 (or_5_out[1], and_7_out, and_8_out, and_9_out, and_10_out);
  or or_5 (or_5_out[0], and_11_out, and_12_out, and_13_out, and_14_out, and_15_out);
  Shift_Register #(.width(4), .length(5), .trigger("falling")) shift_register_1 (
    .in(or_5_out), .clk(or_1_out), .clr(in_3), .q0(shift_register_1_q0), .q1(shift_register_1_q1),
    .q2(shift_register_1_q2), .q3(shift_register_1_q3), .q4(shift_register_1_q4));  // open: shift, out, load, d0, d1, d2, d3, d4
  Digits_to_Binary digits_to_binary_1 (
    .in_1(shift_register_1_q4), .in_2(shift_register_1_q3), .in_3(shift_register_1_q2),
    .in_4(shift_register_1_q1), .in_5(shift_register_1_q0), .out_6(out_12));
endmodule

module _16bit_Display_wreg (
  input  [15:0] in_1,
  output [3:0] out_2,
  output [3:0] out_3,
  output [3:0] out_4,
  output [3:0] out_5,
  output [3:0] out_6
);

  wire or_1_out;
  wire [3:0] n8bits_to_4bits_1_out_2, n8bits_to_4bits_2_out_2, n8bits_to_4bits_3_out_2,
       n8bits_to_4bits_4_out_2, n8bits_to_4bits_5_out_2;
  wire [7:0] n16bits_to_8bits_1_out_2, n16bits_to_8bits_2_out_2, n16bits_to_8bits_3_out_2,
       n16bits_to_8bits_4_out_2, n16bits_to_8bits_5_out_2;
  wire [15:0] divider_1_out, divider_2_out, divider_3_out, divider_4_out, multiplier_1_out, multiplier_2_out,
       multiplier_3_out, multiplier_4_out, subtractor_1_out, subtractor_2_out, subtractor_3_out,
       subtractor_4_out;

  Divider #(.width(16)) divider_1 (.a(in_1), .b(16'h2710), .out(divider_1_out));  // open: upper, rem
  Subtractor #(.width(16)) subtractor_1 (.a(in_1), .b(multiplier_1_out), .out(subtractor_1_out));  // open: bin, bout
  Divider #(.width(16)) divider_2 (.a(subtractor_1_out), .b(16'h3e8), .out(divider_2_out));  // open: upper, rem
  Subtractor #(.width(16)) subtractor_2 (
    .a(subtractor_1_out), .b(multiplier_2_out), .out(subtractor_2_out));  // open: bin, bout
  Divider #(.width(16)) divider_3 (.a(subtractor_2_out), .b(16'h64), .out(divider_3_out));  // open: upper, rem
  Subtractor #(.width(16)) subtractor_3 (
    .a(subtractor_2_out), .b(multiplier_3_out), .out(subtractor_3_out));  // open: bin, bout
  Divider #(.width(16)) divider_4 (.a(subtractor_3_out), .b(16'ha), .out(divider_4_out));  // open: upper, rem
  Subtractor #(.width(16)) subtractor_4 (
    .a(subtractor_3_out), .b(multiplier_4_out), .out(subtractor_4_out));  // open: bin, bout
  Multiplier #(.width(16)) multiplier_1 (.a(divider_1_out), .b(16'h2710), .out(multiplier_1_out));  // open: cin, cout
  Multiplier #(.width(16)) multiplier_2 (.a(divider_2_out), .b(16'h3e8), .out(multiplier_2_out));  // open: cin, cout
  Multiplier #(.width(16)) multiplier_3 (.a(divider_3_out), .b(16'h64), .out(multiplier_3_out));  // open: cin, cout
  Multiplier #(.width(16)) multiplier_4 (.a(divider_4_out), .b(16'ha), .out(multiplier_4_out));  // open: cin, cout
  _16bits_to_8bits u_16bits_to_8bits_1 (.out_2(n16bits_to_8bits_1_out_2), .in_1(divider_1_out));
  _8bits_to_4bits u_8bits_to_4bits_1 (.out_2(n8bits_to_4bits_1_out_2), .in_1(n16bits_to_8bits_1_out_2));
  _8bits_to_4bits u_8bits_to_4bits_2 (.out_2(n8bits_to_4bits_2_out_2), .in_1(n16bits_to_8bits_2_out_2));
  _16bits_to_8bits u_16bits_to_8bits_2 (.out_2(n16bits_to_8bits_2_out_2), .in_1(divider_2_out));
  _8bits_to_4bits u_8bits_to_4bits_3 (.out_2(n8bits_to_4bits_3_out_2), .in_1(n16bits_to_8bits_3_out_2));
  _16bits_to_8bits u_16bits_to_8bits_3 (.out_2(n16bits_to_8bits_3_out_2), .in_1(divider_3_out));
  _8bits_to_4bits u_8bits_to_4bits_4 (.out_2(n8bits_to_4bits_4_out_2), .in_1(n16bits_to_8bits_4_out_2));
  _16bits_to_8bits u_16bits_to_8bits_4 (.out_2(n16bits_to_8bits_4_out_2), .in_1(divider_4_out));
  _16bits_to_8bits u_16bits_to_8bits_5 (.out_2(n16bits_to_8bits_5_out_2), .in_1(subtractor_4_out));
  _8bits_to_4bits u_8bits_to_4bits_5 (.out_2(n8bits_to_4bits_5_out_2), .in_1(n16bits_to_8bits_5_out_2));
  Register #(.width(4), .trigger("high")) register_1 (
    .D(n8bits_to_4bits_1_out_2), .Q(out_2), .clk(or_1_out));  // open: en, clr
  Register #(.width(4), .trigger("high")) register_2 (
    .D(n8bits_to_4bits_2_out_2), .Q(out_3), .clk(or_1_out));  // open: en, clr
  Register #(.width(4), .trigger("high")) register_3 (
    .D(n8bits_to_4bits_3_out_2), .Q(out_4), .clk(or_1_out));  // open: en, clr
  Register #(.width(4), .trigger("high")) register_4 (
    .D(n8bits_to_4bits_4_out_2), .Q(out_5), .clk(or_1_out));  // open: en, clr
  Register #(.width(4), .trigger("high")) register_5 (
    .D(n8bits_to_4bits_5_out_2), .Q(out_6), .clk(or_1_out));  // open: en, clr
  or or_1 (or_1_out, in_1[8], in_1[15], in_1[14], in_1[13], in_1[12], in_1[11], in_1[10], in_1[9], in_1[7], in_1[6], in_1[5], in_1[4], in_1[3], in_1[2], in_1[1], in_1[0]);
endmodule
