// Logisim project CPU.circ as structural Verilog: 1 circuit, main circuit main
module main (
  output [7:0] out_1,
  output [7:0] out_2,
  output [7:0] out_3,
  output [7:0] out_4,
  output [7:0] out_5
);

  wire and_1_out, and_2_out, clock_1_out, not_1_out;
  wire [1:0] rom_1_data;
  wire [2:0] rom_1_data_2, rom_1_data_3;
  wire [7:0] counter_1_q, counter_2_q, demultiplexer_1_out7;

  Clock clock_1 (.out(clock_1_out));
  not not_1 (not_1_out, and_2_out);
  and and_1 (and_1_out, clock_1_out, rom_1_data_2[2], rom_1_data_2[1], rom_1_data_2[0]);
  and and_2 (and_2_out, ~rom_1_data_2[0], ~rom_1_data_2[1], rom_1_data_2[2]);  // AND_Gate
  Counter #(.trigger("falling")) counter_1 (
    .load(and_2_out), .D(out_5), .count(not_1_out), .Q(counter_1_q), .clk(and_1_out));  // open: carry, clr
  Counter counter_2 (.Q(counter_2_q), .clk(clock_1_out));  // open: load, D, count, carry, clr
  RAM #(.bus("separate")) ram_1 (
    .addr(counter_1_q), .din(demultiplexer_1_out7), .data(out_1), .str(and_1_out), .clk(and_1_out));  // open: sel, ld, clr
  ROM #(.dataWidth(16)) rom_1 (
    .addr(counter_2_q), .data({rom_1_data_3, rom_1_data_2, rom_1_data, out_2}));  // open: sel
  Multiplexer #(.select(3), .width(8), .enable("false")) multiplexer_1 (
    .in6(out_2), .in7(out_1), .out(out_3), .sel(rom_1_data_3));  // open: in0, in1, in2, in3, in4, in5
  Demultiplexer #(.select(3), .width(8), .enable("false")) demultiplexer_1 (
    .out4(out_5), .out6(out_4), .out7(demultiplexer_1_out7), .in(out_3), .sel(rom_1_data_2));  // open: out0, out1, out2, out3, out5

  // Notes on the sheet:
  //   contents of rom_1 (hex, n*v repeats v):
  //   dc68 dc65 dc6c dc6c dc6f dc77 dc6f dc72 dc6c dc64 d000 f400 f401 f402 f403 f404 f405 f406 f407 f408
  //   f409
endmodule
