// Logisim project CPU_backup.circ as structural Verilog: 5 circuits, main circuit main
module main (
  output [7:0] out_1,
  output [7:0] out_2,
  output [7:0] out_3
);

  wire ALU1, ALU2, and_1_out, and_2_out, clock_1_out, not_1_out, REG1;
  wire [1:0] data_splitter_1_out_4;
  wire [2:0] data_splitter_1_out_2, data_splitter_1_out_3;
  wire [3:0] n16bit_display_1_out_2, n16bit_display_1_out_3, n16bit_display_1_out_4, n16bit_display_1_out_5,
       n16bit_display_1_out_6;
  wire [6:0] bit_extender_1_out;
  wire [7:0] alu_1_out_4, counter_1_q, data_splitter_1_out_5, demultiplexer_1_out0, demultiplexer_1_out1,
       demultiplexer_1_out5, demultiplexer_1_out6, demultiplexer_1_out7, multiplexer_1_out, ram_1_data,
       register_1_q, register_2_q, register_3_q, register_6_q;
  wire [15:0] n8bits_to_16bits_1_out_2, rom_1_data;

  Clock clock_1 (.out(clock_1_out));
  not not_1 (not_1_out, and_1_out);
  and and_1 (and_1_out, ~data_splitter_1_out_3[2], ~data_splitter_1_out_3[1], ~data_splitter_1_out_3[0]);  // AND_Gate
  Counter counter_1 (
    .load(and_1_out), .D(demultiplexer_1_out0), .count(not_1_out), .Q(counter_1_q), .clk(clock_1_out));  // open: carry, clr
  Register register_1 (.D(demultiplexer_1_out1), .Q(register_1_q), .clk(clock_1_out));  // open: en, clr
  and and_2 (and_2_out, ~data_splitter_1_out_3[0], data_splitter_1_out_3[1], ~data_splitter_1_out_3[2]);  // AND_Gate
  and and_3 (ALU2, data_splitter_1_out_3[0], data_splitter_1_out_3[1], data_splitter_1_out_3[2]);
  and and_4 (ALU1, ~data_splitter_1_out_3[0], data_splitter_1_out_3[1], data_splitter_1_out_3[2]);  // AND_Gate
  and and_5 (REG1, ~data_splitter_1_out_3[0], ~data_splitter_1_out_3[1], data_splitter_1_out_3[2]);  // AND_Gate
  data_splitter data_splitter_1 (
    .in_1(rom_1_data), .out_2(data_splitter_1_out_2), .out_3(data_splitter_1_out_3),
    .out_4(data_splitter_1_out_4), .out_5(data_splitter_1_out_5));
  ROM #(.dataWidth(16)) rom_1 (.addr(counter_1_q), .data(rom_1_data));  // open: sel
  RAM #(.bus("separate")) ram_1 (
    .addr(register_1_q), .din(out_3), .data(ram_1_data), .str(and_2_out), .clk(clock_1_out));  // open: sel, ld, clr
  Multiplexer #(.select(3), .width(8), .enable("false")) multiplexer_1 (
    .in0(data_splitter_1_out_5), .in1(ram_1_data), .in2(register_6_q), .out(multiplexer_1_out),
    .sel(data_splitter_1_out_2));  // open: in3, in4, in5, in6, in7
  Demultiplexer #(.select(3), .width(8), .enable("false")) demultiplexer_1 (
    .out0(demultiplexer_1_out0), .out1(demultiplexer_1_out1), .out2(out_3), .out3(out_2), .out4(out_1),
    .out5(demultiplexer_1_out5), .out6(demultiplexer_1_out6), .out7(demultiplexer_1_out7),
    .in(multiplexer_1_out), .sel(data_splitter_1_out_3));
  Bit_Extender #(.out_width(7)) bit_extender_1 (.in(out_2), .out(bit_extender_1_out));
  TTY tty_1 (.data(bit_extender_1_out), .clk(clock_1_out));  // open: we, clr
  _8bits_to_16bits u_8bits_to_16bits_1 (.in_1(out_2), .out_2(n8bits_to_16bits_1_out_2));
  Register #(.trigger("falling")) register_2 (.D(demultiplexer_1_out7), .Q(register_2_q), .clk(ALU2));  // open: en, clr
  Register #(.trigger("falling")) register_3 (.D(demultiplexer_1_out6), .Q(register_3_q), .clk(ALU1));  // open: en, clr
  Register register_4 (.D(demultiplexer_1_out5));  // open: en, Q, clk, clr
  Register #(.trigger("falling")) register_5 (.D(out_1), .clk(REG1));  // open: en, Q, clr
  // OR_Gate or_1 has open pins: in0=data_splitter_1_out_4[0], in1=data_splitter_1_out_4[1], out=open
  ALU alu_1 (.in_1(register_2_q), .in_2(register_3_q), .in_3(data_splitter_1_out_4), .out_4(alu_1_out_4));
  Register register_6 (.D(alu_1_out_4), .Q(register_6_q), .clk(clock_1_out));  // open: en, clr
  Hex_Digit_Display hex_digit_display_1 (.value(n16bit_display_1_out_3));  // open: dp
  Hex_Digit_Display hex_digit_display_2 (.value(n16bit_display_1_out_2));  // open: dp
  _16bit_Display u_16bit_display_1 (
    .in_1(n8bits_to_16bits_1_out_2), .out_2(n16bit_display_1_out_2), .out_3(n16bit_display_1_out_3),
    .out_4(n16bit_display_1_out_4), .out_5(n16bit_display_1_out_5), .out_6(n16bit_display_1_out_6));
  Hex_Digit_Display hex_digit_display_3 (.value(n16bit_display_1_out_4));  // open: dp
  Hex_Digit_Display hex_digit_display_4 (.value(n16bit_display_1_out_5));  // open: dp
  Hex_Digit_Display hex_digit_display_5 (.value(n16bit_display_1_out_6));  // open: dp

  // Notes on the sheet:
  //   contents of rom_1 (hex, n*v repeats v):
  //   400 801 400 3800 401 3c00 401 4800 401 3000
endmodule

// SPLIT
module data_splitter (
  input  [15:0] in_1,
  output [2:0] out_2,
  output [2:0] out_3,
  output [1:0] out_4,
  output [7:0] out_5
);


  assign out_2 = in_1[15:13];
  assign out_3 = in_1[12:10];
  assign out_4 = in_1[9:8];
  assign out_5 = in_1[7:0];
endmodule

module ALU (
  input  [7:0] in_1,
  input  [7:0] in_2,
  input  [1:0] in_3,
  output [7:0] out_4
);

  wire [7:0] adder_1_out, divider_1_out, multiplier_1_out, subtractor_1_out;

  Adder adder_1 (.a(in_1), .b(in_2), .out(adder_1_out));  // open: cin, cout
  Subtractor subtractor_1 (.a(in_1), .b(in_2), .out(subtractor_1_out));  // open: bin, bout
  Multiplier multiplier_1 (.a(in_1), .b(in_2), .out(multiplier_1_out));  // open: cin, cout
  Divider divider_1 (.a(in_1), .b(in_2), .out(divider_1_out));  // open: upper, rem
  Multiplexer #(.select(2), .width(8), .enable("false")) multiplexer_1 (
    .in0(adder_1_out), .in1(subtractor_1_out), .in2(multiplier_1_out), .in3(divider_1_out), .out(out_4),
    .sel(in_3));
endmodule

module CPU (
  input  Clock,
  input  [15:0] Memory_in,
  input  [7:0] RAM_data_OUT,
  output [7:0] Memory_out,
  output [7:0] REG2,
  output [7:0] Address,
  output [7:0] RAM_data_IN,
  output [7:0] REG1,
  output RAM_store,
  output [6:0] TTY_out
);

  wire ALU1, ALU2, and_1_out, not_1_out, REG1_t;
  wire [1:0] data_splitter_1_out_4;
  wire [2:0] data_splitter_1_out_2, data_splitter_1_out_3;
  wire [7:0] alu_1_out_4, data_splitter_1_out_5, demultiplexer_1_out0, demultiplexer_1_out1,
       demultiplexer_1_out3, demultiplexer_1_out4, demultiplexer_1_out5, demultiplexer_1_out6,
       demultiplexer_1_out7, multiplexer_1_out, register_2_q, register_3_q, register_6_q;

  not not_1 (not_1_out, and_1_out);
  and and_1 (and_1_out, ~data_splitter_1_out_3[2], ~data_splitter_1_out_3[1], ~data_splitter_1_out_3[0]);  // AND_Gate
  Counter counter_1 (
    .load(and_1_out), .D(demultiplexer_1_out0), .count(not_1_out), .Q(Memory_out), .clk(Clock));  // open: carry, clr
  Register register_1 (.D(demultiplexer_1_out1), .Q(Address), .clk(Clock));  // open: en, clr
  and and_2 (RAM_store, ~data_splitter_1_out_3[0], data_splitter_1_out_3[1], ~data_splitter_1_out_3[2]);  // AND_Gate
  and and_3 (ALU2, data_splitter_1_out_3[0], data_splitter_1_out_3[1], data_splitter_1_out_3[2]);
  and and_4 (ALU1, ~data_splitter_1_out_3[0], data_splitter_1_out_3[1], data_splitter_1_out_3[2]);  // AND_Gate
  and and_5 (REG1_t, ~data_splitter_1_out_3[0], ~data_splitter_1_out_3[1], data_splitter_1_out_3[2]);  // AND_Gate
  data_splitter data_splitter_1 (
    .in_1(Memory_in), .out_2(data_splitter_1_out_2), .out_3(data_splitter_1_out_3),
    .out_4(data_splitter_1_out_4), .out_5(data_splitter_1_out_5));
  Multiplexer #(.select(3), .width(8), .enable("false")) multiplexer_1 (
    .in0(data_splitter_1_out_5), .in1(RAM_data_OUT), .in2(register_6_q), .out(multiplexer_1_out),
    .sel(data_splitter_1_out_2));  // open: in3, in4, in5, in6, in7
  Demultiplexer #(.select(3), .width(8), .enable("false")) demultiplexer_1 (
    .out0(demultiplexer_1_out0), .out1(demultiplexer_1_out1), .out2(RAM_data_IN),
    .out3(demultiplexer_1_out3), .out4(demultiplexer_1_out4), .out5(demultiplexer_1_out5),
    .out6(demultiplexer_1_out6), .out7(demultiplexer_1_out7), .in(multiplexer_1_out),
    .sel(data_splitter_1_out_3));
  Bit_Extender #(.out_width(7)) bit_extender_1 (.in(demultiplexer_1_out3), .out(TTY_out));
  Register #(.trigger("falling")) register_2 (.D(demultiplexer_1_out7), .Q(register_2_q), .clk(ALU2));  // open: en, clr
  Register #(.trigger("falling")) register_3 (.D(demultiplexer_1_out6), .Q(register_3_q), .clk(ALU1));  // open: en, clr
  Register register_4 (.D(demultiplexer_1_out5), .Q(REG2));  // open: en, clk, clr
  Register #(.trigger("falling")) register_5 (.D(demultiplexer_1_out4), .Q(REG1), .clk(REG1_t));  // open: en, clr
  // OR_Gate or_1 has open pins: in0=data_splitter_1_out_4[0], in1=data_splitter_1_out_4[1], out=open
  ALU alu_1 (.in_1(register_2_q), .in_2(register_3_q), .in_3(data_splitter_1_out_4), .out_4(alu_1_out_4));
  Register register_6 (.D(alu_1_out_4), .Q(register_6_q), .clk(Clock));  // open: en, clr
endmodule

module Test (
  output [7:0] out_1
);

  wire clock_1_out, cpu_1_ram_store;
  wire [3:0] n16bit_display_1_out_2, n16bit_display_1_out_3, n16bit_display_1_out_4, n16bit_display_1_out_5,
       n16bit_display_1_out_6;
  wire [6:0] cpu_1_tty_out;
  wire [7:0] cpu_1_address, cpu_1_memory_out, cpu_1_ram_data_in, ram_1_data;
  wire [15:0] n8bits_to_16bits_1_out_2, rom_1_data;

  Clock clock_1 (.out(clock_1_out));
  CPU cpu_1 (
    .Memory_out(cpu_1_memory_out), .Memory_in(rom_1_data), .REG1(out_1), .TTY_out(cpu_1_tty_out),
    .Clock(clock_1_out), .Address(cpu_1_address), .RAM_data_IN(cpu_1_ram_data_in),
    .RAM_store(cpu_1_ram_store), .RAM_data_OUT(ram_1_data));  // open: REG2
  ROM #(.dataWidth(16)) rom_1 (.addr(cpu_1_memory_out), .data(rom_1_data));  // open: sel
  RAM #(.bus("separate")) ram_1 (
    .addr(cpu_1_address), .din(cpu_1_ram_data_in), .data(ram_1_data), .str(cpu_1_ram_store), .clk(clock_1_out));  // open: sel, ld, clr
  _8bits_to_16bits u_8bits_to_16bits_1 (.in_1(out_1), .out_2(n8bits_to_16bits_1_out_2));
  TTY tty_1 (.data(cpu_1_tty_out), .clk(clock_1_out));  // open: we, clr
  Hex_Digit_Display hex_digit_display_1 (.value(n16bit_display_1_out_3));  // open: dp
  Hex_Digit_Display hex_digit_display_2 (.value(n16bit_display_1_out_2));  // open: dp
  _16bit_Display u_16bit_display_1 (
    .in_1(n8bits_to_16bits_1_out_2), .out_2(n16bit_display_1_out_2), .out_3(n16bit_display_1_out_3),
    .out_4(n16bit_display_1_out_4), .out_5(n16bit_display_1_out_5), .out_6(n16bit_display_1_out_6));
  Hex_Digit_Display hex_digit_display_3 (.value(n16bit_display_1_out_4));  // open: dp
  Hex_Digit_Display hex_digit_display_4 (.value(n16bit_display_1_out_5));  // open: dp
  Hex_Digit_Display hex_digit_display_5 (.value(n16bit_display_1_out_6));  // open: dp

  // Notes on the sheet:
  //   contents of rom_1 (hex, n*v repeats v):
  //   400 801 400 3800 401 3c00 401 4800 401 3000
endmodule
