// Logisim project CPU.circ as structural Verilog
module CPU_v1 (
);

  wire ALU_Ope_Reg, ALU_Reg_A, ALU_Reg_B, clk, not_1_out, OUT1w, OUT2w, OUT3w, OUT4w, RAE, RAM_Addr_act,
       REG1w, REG2w, REG3w, REG4w, we;
  wire [3:0] n16bit_display_1_out_2, n16bit_display_1_out_3, n16bit_display_1_out_4, n16bit_display_1_out_5,
       n16bit_display_1_out_6;
  wire [15:0] alu_1_out_4, ALU_A, ALU_B, ALU_Ope, demultiplexer_1_out3, demultiplexer_1_out4,
       demultiplexer_1_out5, demultiplexer_1_out6, demultiplexer_1_out7, demultiplexer_1_out8,
       demultiplexer_1_out9, demultiplexer_1_out10, demultiplexer_1_out11, demultiplexer_1_out12,
       demultiplexer_1_out13, multiplexer_1_out, OUT1, OUT2, OUT3, OUT4, RAM_addr, RAM_data_in, RAM_data_out,
       REG1, REG2, REG3, REG4, register_1_q, register_13_q, ROM_addr, ROM_addr_out;
  wire [31:0] ROM_data;

  Clock clock_1 (.out(clk));
  and and_1 (RAE, ~ROM_data[26], ~ROM_data[25], ~ROM_data[24], ~ROM_data[23], ~ROM_data[22]);  // AND_Gate
  and and_2 (we, ~ROM_data[26], ~ROM_data[25], ~ROM_data[24], ROM_data[23], ~ROM_data[22]);  // AND_Gate
  and and_3 (ALU_Ope_Reg, ~ROM_data[26], ~ROM_data[25], ~ROM_data[24], ROM_data[23], ROM_data[22]);  // AND_Gate
  and and_4 (ALU_Reg_A, ~ROM_data[26], ~ROM_data[25], ROM_data[24], ~ROM_data[23], ~ROM_data[22]);  // AND_Gate
  and and_5 (ALU_Reg_B, ~ROM_data[26], ~ROM_data[25], ROM_data[24], ~ROM_data[23], ROM_data[22]);  // AND_Gate
  and and_6 (RAM_Addr_act, ~ROM_data[26], ~ROM_data[25], ~ROM_data[24], ~ROM_data[23], ROM_data[22]);  // AND_Gate
  and and_7 (OUT1w, ~ROM_data[26], ~ROM_data[25], ROM_data[24], ROM_data[23], ~ROM_data[22]);  // AND_Gate
  and and_8 (OUT2w, ~ROM_data[26], ~ROM_data[25], ROM_data[24], ROM_data[23], ROM_data[22]);  // AND_Gate
  and and_9 (OUT3w, ~ROM_data[26], ROM_data[25], ~ROM_data[24], ~ROM_data[23], ~ROM_data[22]);  // AND_Gate
  and and_10 (OUT4w, ~ROM_data[26], ROM_data[25], ~ROM_data[24], ~ROM_data[23], ROM_data[22]);  // AND_Gate
  and and_11 (REG1w, ~ROM_data[26], ROM_data[25], ~ROM_data[24], ROM_data[23], ~ROM_data[22]);  // AND_Gate
  and and_12 (REG2w, ~ROM_data[26], ROM_data[25], ~ROM_data[24], ROM_data[23], ROM_data[22]);  // AND_Gate
  and and_13 (REG3w, ~ROM_data[26], ROM_data[25], ROM_data[24], ~ROM_data[23], ~ROM_data[22]);  // AND_Gate
  and and_14 (REG4w, ~ROM_data[26], ROM_data[25], ROM_data[24], ~ROM_data[23], ROM_data[22]);  // AND_Gate
  Register #(.width(16), .trigger("falling")) register_1 (
    .D(RAM_addr), .Q(register_1_q), .clk(RAM_Addr_act));  // open: en, clr
  ROM #(.addrWidth(16), .dataWidth(32)) rom_1 (.addr(ROM_addr_out), .data(ROM_data));  // open: sel
  RAM #(.addrWidth(16), .dataWidth(16), .bus("separate")) ram_1 (
    .addr(register_1_q), .din(RAM_data_in), .data(RAM_data_out), .str(we), .clk(clk));  // open: sel, ld, clr
  not not_1 (not_1_out, RAE);
  Counter #(.width(16), .max('hffff), .trigger("falling")) counter_1 (
    .load(RAE), .D(ROM_addr), .count(not_1_out), .Q(ROM_addr_out), .clk(clk));  // open: carry, clr
  Hex_Digit_Display hex_digit_display_1 (.value(n16bit_display_1_out_2));  // open: dp
  _16bit_Display u_16bit_display_1 (
    .in_1(OUT1), .out_2(n16bit_display_1_out_2), .out_3(n16bit_display_1_out_3),
    .out_4(n16bit_display_1_out_4), .out_5(n16bit_display_1_out_5), .out_6(n16bit_display_1_out_6));
  Hex_Digit_Display hex_digit_display_2 (.value(n16bit_display_1_out_4));  // open: dp
  Hex_Digit_Display hex_digit_display_3 (.value(n16bit_display_1_out_3));  // open: dp
  Demultiplexer #(.select(5), .width(16), .enable("false")) demultiplexer_1 (
    .out0(ROM_addr), .out1(RAM_addr), .out2(RAM_data_in), .out3(demultiplexer_1_out3),
    .out4(demultiplexer_1_out4), .out5(demultiplexer_1_out5), .out6(demultiplexer_1_out6),
    .out7(demultiplexer_1_out7), .out8(demultiplexer_1_out8), .out9(demultiplexer_1_out9),
    .out10(demultiplexer_1_out10), .out11(demultiplexer_1_out11), .out12(demultiplexer_1_out12),
    .out13(demultiplexer_1_out13), .in(multiplexer_1_out), .sel(ROM_data[26:22]));  // open: out14, out15, out16, out17, out18, out19, out20, out21, out22, out23, out24, out25, out26, out27, out28, out29, out30, out31
  Multiplexer #(.select(5), .width(16), .enable("false")) multiplexer_1 (
    .in0(ROM_data[15:0]), .in1(RAM_data_out), .in2(register_13_q), .in3(REG1), .in4(REG2), .in5(REG3),
    .in6(REG4), .out(multiplexer_1_out), .sel(ROM_data[31:27]));  // open: in7, in8, in9, in10, in11, in12, in13, in14, in15, in16, in17, in18, in19, in20, in21, in22, in23, in24, in25, in26, in27, in28, in29, in30, in31
  Register #(.width(16), .trigger("low")) register_2 (
    .D(demultiplexer_1_out9), .Q(OUT4), .clk(OUT4w));  // open: en, clr
  Register #(.width(16), .trigger("falling")) register_3 (
    .D(demultiplexer_1_out8), .Q(OUT3), .clk(OUT3w));  // open: en, clr
  Register #(.width(16), .trigger("falling")) register_4 (
    .D(demultiplexer_1_out7), .Q(OUT2), .clk(OUT2w));  // open: en, clr
  Register #(.width(16), .trigger("falling")) register_5 (
    .D(demultiplexer_1_out6), .Q(OUT1), .clk(OUT1w));  // open: en, clr
  Register #(.width(16), .trigger("falling")) register_6 (
    .D(demultiplexer_1_out5), .Q(ALU_B), .clk(ALU_Reg_B));  // open: en, clr
  Register #(.width(16), .trigger("falling")) register_7 (
    .D(demultiplexer_1_out4), .Q(ALU_A), .clk(ALU_Reg_A));  // open: en, clr
  Register #(.width(16), .trigger("falling")) register_8 (
    .D(demultiplexer_1_out3), .Q(ALU_Ope), .clk(ALU_Ope_Reg));  // open: en, clr
  Hex_Digit_Display hex_digit_display_4 (.value(n16bit_display_1_out_6));  // open: dp
  Hex_Digit_Display hex_digit_display_5 (.value(n16bit_display_1_out_5));  // open: dp
  Register #(.width(16), .trigger("low")) register_9 (
    .D(demultiplexer_1_out13), .Q(REG4), .clk(REG4w));  // open: en, clr
  Register #(.width(16), .trigger("falling")) register_10 (
    .D(demultiplexer_1_out12), .Q(REG3), .clk(REG3w));  // open: en, clr
  Register #(.width(16), .trigger("falling")) register_11 (
    .D(demultiplexer_1_out11), .Q(REG2), .clk(REG2w));  // open: en, clr
  Register #(.width(16), .trigger("falling")) register_12 (
    .D(demultiplexer_1_out10), .Q(REG1), .clk(REG1w));  // open: en, clr
  ALU alu_1 (.in_1(ALU_A), .in_2(ALU_B), .in_3(ALU_Ope), .out_4(alu_1_out_4));
  Register #(.width(16)) register_13 (.D(alu_1_out_4), .Q(register_13_q), .clk(clk));  // open: en, clr

  // Notes on the sheet:
  //   from
  //   contents of rom_1 (hex, n*v repeats v):
  //   400000 800001 400000 9000000 400001 9400000 400001 10800000 400001 9800000 400001 8400000 80ffff 2
  //   to
  //   data
  //   RAE=ROM Address enabled
endmodule

module ALU (
  input  [15:0] in_1,
  input  [15:0] in_2,
  input  [15:0] in_3,
  output [15:0] out_4
);

  wire [4:0] bit_extender_1_out;
  wire [15:0] adder_1_out, divider_1_out, multiplier_1_out, subtractor_1_out;

  Adder #(.width(16)) adder_1 (.a(in_1), .b(in_2), .out(adder_1_out));  // open: cin, cout
  Subtractor #(.width(16)) subtractor_1 (.a(in_1), .b(in_2), .out(subtractor_1_out));  // open: bin, bout
  Multiplier #(.width(16)) multiplier_1 (.a(in_1), .b(in_2), .out(multiplier_1_out));  // open: cin, cout
  Divider #(.width(16)) divider_1 (.a(in_1), .b(in_2), .out(divider_1_out));  // open: upper, rem
  Bit_Extender #(.in_width(16), .out_width(5)) bit_extender_1 (.in(in_3), .out(bit_extender_1_out));
  Multiplexer #(.select(5), .width(16), .enable("false")) multiplexer_1 (
    .in0(adder_1_out), .in1(subtractor_1_out), .in2(multiplier_1_out), .in3(divider_1_out), .out(out_4),
    .sel(bit_extender_1_out));  // open: in4, in5, in6, in7, in8, in9, in10, in11, in12, in13, in14, in15, in16, in17, in18, in19, in20, in21, in22, in23, in24, in25, in26, in27, in28, in29, in30, in31
endmodule

module write_selector (
  input  in_1,
  input  in_2,
  input  in_3,
  input  in_4,
  input  in_5,
  output out_6,
  output out_7,
  output out_8,
  output out_9,
  output out_10,
  output out_11,
  output out_12,
  output out_13,
  output out_14,
  output out_15,
  output out_16,
  output out_17,
  output out_18,
  output out_19,
  output out_20,
  output out_21,
  output out_22,
  output out_23,
  output out_24,
  output out_25,
  output out_26,
  output out_27,
  output out_28,
  output out_29,
  output out_30,
  output out_31,
  output out_32,
  output out_33,
  output out_34,
  output out_35,
  output out_36,
  output out_37
);

  write_selector_0_11 write_selector_0_11_1 (
    .a(in_1), .b(in_2), .c(in_3), .d(in_4), .e(in_5), .x(out_17), .y(out_16), .z(out_15), .u(out_14),
    .v(out_13), .w(out_12), .s(out_11), .t(out_10), .x2(out_9), .x3(out_8), .x4(out_7), .x5(out_6));
  write_selector_12_23 write_selector_12_23_1 (
    .a(in_1), .b(in_2), .c(in_3), .d(in_4), .e(in_5), .x(out_29), .y(out_28), .z(out_27), .u(out_26),
    .v(out_25), .w(out_24), .s(out_23), .t(out_22), .x2(out_21), .x3(out_20), .x4(out_19), .x5(out_18));
  write_selector_24_31 write_selector_24_31_1 (
    .a(in_1), .b(in_2), .c(in_3), .d(in_4), .e(in_5), .x(out_30), .y(out_31), .z(out_32), .u(out_33),
    .v(out_34), .w(out_35), .s(out_36), .t(out_37));
endmodule

module write_selector_0_11 (
  input  a,
  input  b,
  input  c,
  input  d,
  input  e,
  output x,
  output y,
  output z,
  output u,
  output v,
  output w,
  output s,
  output t,
  output x2,
  output x3,
  output x4,
  output x5
);

  wire not_1_out, not_2_out, not_3_out, not_4_out, not_5_out, not_6_out, not_7_out, not_8_out, not_9_out,
       not_10_out, not_11_out, not_12_out, not_13_out, not_14_out, not_15_out, not_16_out, not_17_out,
       not_18_out, not_19_out, not_20_out, not_21_out, not_22_out, not_23_out, not_24_out, not_25_out,
       not_26_out, not_27_out, not_28_out, not_29_out, not_30_out, not_31_out, not_32_out, not_33_out,
       not_34_out, not_35_out, not_36_out, not_37_out, not_38_out, not_39_out, not_40_out;

  not not_1 (not_1_out, a);
  not not_2 (not_2_out, c);
  not not_3 (not_3_out, a);
  not not_4 (not_4_out, c);
  not not_5 (not_5_out, e);
  not not_6 (not_6_out, a);
  not not_7 (not_7_out, c);
  not not_8 (not_8_out, d);
  not not_9 (not_9_out, a);
  not not_10 (not_10_out, c);
  not not_11 (not_11_out, d);
  not not_12 (not_12_out, e);
  not not_13 (not_13_out, a);
  not not_14 (not_14_out, b);
  not not_15 (not_15_out, a);
  not not_16 (not_16_out, b);
  not not_17 (not_17_out, e);
  not not_18 (not_18_out, a);
  not not_19 (not_19_out, b);
  not not_20 (not_20_out, d);
  not not_21 (not_21_out, a);
  not not_22 (not_22_out, b);
  not not_23 (not_23_out, d);
  not not_24 (not_24_out, e);
  not not_25 (not_25_out, a);
  not not_26 (not_26_out, b);
  not not_27 (not_27_out, c);
  not not_28 (not_28_out, a);
  not not_29 (not_29_out, b);
  not not_30 (not_30_out, c);
  not not_31 (not_31_out, e);
  not not_32 (not_32_out, a);
  not not_33 (not_33_out, b);
  not not_34 (not_34_out, c);
  not not_35 (not_35_out, d);
  not not_36 (not_36_out, a);
  not not_37 (not_37_out, b);
  not not_38 (not_38_out, c);
  not not_39 (not_39_out, d);
  not not_40 (not_40_out, e);
  and and_1 (x, not_1_out, b, not_2_out, d, e);
  and and_2 (y, not_3_out, b, not_4_out, d, not_5_out);
  and and_3 (z, not_6_out, b, not_7_out, not_8_out, e);
  and and_4 (u, not_9_out, b, not_10_out, not_11_out, not_12_out);
  and and_5 (v, not_13_out, not_14_out, c, d, e);
  and and_6 (w, not_15_out, not_16_out, c, d, not_17_out);
  and and_7 (s, not_18_out, not_19_out, c, not_20_out, e);
  and and_8 (t, not_21_out, not_22_out, c, not_23_out, not_24_out);
  and and_9 (x2, not_25_out, not_26_out, not_27_out, d, e);
  and and_10 (x3, not_28_out, not_29_out, not_30_out, d, not_31_out);
  and and_11 (x4, not_32_out, not_33_out, not_34_out, not_35_out, e);
  and and_12 (x5, not_36_out, not_37_out, not_38_out, not_39_out, not_40_out);
endmodule

module write_selector_12_23 (
  input  a,
  input  b,
  input  c,
  input  d,
  input  e,
  output x,
  output y,
  output z,
  output u,
  output v,
  output w,
  output s,
  output t,
  output x2,
  output x3,
  output x4,
  output x5
);

  wire not_1_out, not_2_out, not_3_out, not_4_out, not_5_out, not_6_out, not_7_out, not_8_out, not_9_out,
       not_10_out, not_11_out, not_12_out, not_13_out, not_14_out, not_15_out, not_16_out, not_17_out,
       not_18_out, not_19_out, not_20_out, not_21_out, not_22_out, not_23_out, not_24_out, not_25_out,
       not_26_out, not_27_out, not_28_out;

  not not_1 (not_1_out, b);
  not not_2 (not_2_out, b);
  not not_3 (not_3_out, e);
  not not_4 (not_4_out, b);
  not not_5 (not_5_out, d);
  not not_6 (not_6_out, b);
  not not_7 (not_7_out, d);
  not not_8 (not_8_out, e);
  not not_9 (not_9_out, b);
  not not_10 (not_10_out, c);
  not not_11 (not_11_out, b);
  not not_12 (not_12_out, c);
  not not_13 (not_13_out, e);
  not not_14 (not_14_out, b);
  not not_15 (not_15_out, c);
  not not_16 (not_16_out, d);
  not not_17 (not_17_out, b);
  not not_18 (not_18_out, c);
  not not_19 (not_19_out, d);
  not not_20 (not_20_out, e);
  not not_21 (not_21_out, a);
  not not_22 (not_22_out, a);
  not not_23 (not_23_out, e);
  not not_24 (not_24_out, a);
  not not_25 (not_25_out, d);
  not not_26 (not_26_out, a);
  not not_27 (not_27_out, d);
  not not_28 (not_28_out, e);
  and and_1 (x, a, not_1_out, c, d, e);
  and and_2 (y, a, not_2_out, c, d, not_3_out);
  and and_3 (z, a, not_4_out, c, not_5_out, e);
  and and_4 (u, a, not_6_out, c, not_7_out, not_8_out);
  and and_5 (v, a, not_9_out, not_10_out, d, e);
  and and_6 (w, a, not_11_out, not_12_out, d, not_13_out);
  and and_7 (s, a, not_14_out, not_15_out, not_16_out, e);
  and and_8 (t, a, not_17_out, not_18_out, not_19_out, not_20_out);
  and and_9 (x2, not_21_out, b, c, d, e);
  and and_10 (x3, not_22_out, b, c, d, not_23_out);
  and and_11 (x4, not_24_out, b, c, not_25_out, e);
  and and_12 (x5, not_26_out, b, c, not_27_out, not_28_out);
endmodule

module write_selector_24_31 (
  input  a,
  input  b,
  input  c,
  input  d,
  input  e,
  output x,
  output y,
  output z,
  output u,
  output v,
  output w,
  output s,
  output t
);

  wire not_1_out, not_2_out, not_3_out, not_4_out, not_5_out, not_6_out, not_7_out, not_8_out, not_9_out,
       not_10_out, not_11_out, not_12_out;

  and and_1 (x, a, b, c, d, e);
  not not_1 (not_1_out, e);
  not not_2 (not_2_out, d);
  not not_3 (not_3_out, d);
  not not_4 (not_4_out, e);
  not not_5 (not_5_out, c);
  not not_6 (not_6_out, c);
  not not_7 (not_7_out, e);
  not not_8 (not_8_out, c);
  not not_9 (not_9_out, d);
  not not_10 (not_10_out, c);
  not not_11 (not_11_out, d);
  not not_12 (not_12_out, e);
  and and_2 (y, a, b, c, d, not_1_out);
  and and_3 (z, a, b, c, not_2_out, e);
  and and_4 (u, a, b, c, not_3_out, not_4_out);
  and and_5 (v, a, b, not_5_out, d, e);
  and and_6 (w, a, b, not_6_out, d, not_7_out);
  and and_7 (s, a, b, not_8_out, not_9_out, e);
  and and_8 (t, a, b, not_10_out, not_11_out, not_12_out);
endmodule
