// Logisim project Display module.circ as structural Verilog: 13 circuits, main circuit Test circuit
module main (
  output [2:0] out_1
);

  wire _0_out, _1_out, _2_out, _3_out, _4_out, _5_out, _6_out, _7_out, _8_out, _9_out, button_1_out,
       button_2_out, button_3_out, button_4_out, button_5_out, C_out, keyboard_1_out_18, undriven;
  wire [3:0] display_driver_1_out_2, display_driver_1_out_3, display_driver_1_out_4, display_driver_1_out_5,
       display_driver_1_out_6, undriven_2, undriven_3, undriven_4, undriven_5, undriven_6;
  wire [7:0] keyboard_1_out_17;
  wire [15:0] bcd_to_16bits_1_out_5;

  Button _7 (.out(_7_out));
  Button _8 (.out(_8_out));
  Button _4 (.out(_4_out));
  Button _5 (.out(_5_out));
  Button _2 (.out(_2_out));
  Button _1 (.out(_1_out));
  Button _0 (.out(_0_out));
  Button _9 (.out(_9_out));
  Button _6 (.out(_6_out));
  Button _3 (.out(_3_out));
  Button C (.out(C_out));
  Button button_1 (.out(button_1_out));
  Button button_2 (.out(button_2_out));
  Button button_3 (.out(button_3_out));
  Button button_4 (.out(button_4_out));
  Button button_5 (.out(button_5_out));
  keyboard keyboard_1 (
    .in_6(_9_out), .in_7(_8_out), .in_8(_7_out), .in_9(_6_out), .in_10(_5_out), .in_11(_4_out),
    .in_12(_3_out), .in_13(_2_out), .in_14(_1_out), .in_15(_0_out), .in_2(button_4_out), .in_1(button_5_out),
    .in_3(button_3_out), .in_4(button_2_out), .in_5(button_1_out), .out_16(out_1),
    .out_17(keyboard_1_out_17), .out_18(keyboard_1_out_18));
  bcd_to_16bits bcd_to_16bits_1 (
    .clk(undriven), .in_2(keyboard_1_out_17), .in_3(keyboard_1_out_18), .in_4(C_out),
    .out_5(bcd_to_16bits_1_out_5));
  Hex_Digit_Display hex_digit_display_1 (.value(display_driver_1_out_2));  // open: dp
  display_driver display_driver_1 (
    .in_1(bcd_to_16bits_1_out_5), .out_2(display_driver_1_out_2), .out_3(display_driver_1_out_3),
    .out_4(display_driver_1_out_4), .out_5(display_driver_1_out_5), .out_6(display_driver_1_out_6));
  Hex_Digit_Display hex_digit_display_2 (.value(undriven_2));  // open: dp
  Hex_Digit_Display hex_digit_display_3 (.value(display_driver_1_out_3));  // open: dp
  Hex_Digit_Display hex_digit_display_4 (.value(display_driver_1_out_4));  // open: dp
  Hex_Digit_Display hex_digit_display_5 (.value(undriven_3));  // open: dp
  Hex_Digit_Display hex_digit_display_6 (.value(undriven_6));  // open: dp
  Hex_Digit_Display hex_digit_display_7 (.value(display_driver_1_out_5));  // open: dp
  Hex_Digit_Display hex_digit_display_8 (.value(display_driver_1_out_6));  // open: dp
  Hex_Digit_Display hex_digit_display_9 (.value(undriven_4));  // open: dp
  Hex_Digit_Display hex_digit_display_10 (.value(undriven_5));  // open: dp
endmodule

module display_driver (
  input  [15:0] in_1,
  output [3:0] out_2,
  output [3:0] out_3,
  output [3:0] out_4,
  output [3:0] out_5,
  output [3:0] out_6
);

  wire [15:0] multiplier_1_out, multiplier_2_out, multiplier_3_out, multiplier_4_out, multiplier_5_out,
       subtractor_1_out, subtractor_2_out, subtractor_3_out, subtractor_4_out;
  wire [15:4] divider_1_out, divider_2_out, divider_3_out, divider_4_out, divider_5_out;

  Divider #(.width(16)) divider_1 (.a(in_1), .b(16'h2710), .out({divider_1_out, out_2}));  // open: upper, rem
  Multiplier #(.width(16)) multiplier_1 (
    .a({divider_1_out, out_2}), .b(16'h2710), .out(multiplier_1_out));  // open: cin, cout
  Subtractor #(.width(16)) subtractor_1 (.a(in_1), .b(multiplier_1_out), .out(subtractor_1_out));  // open: bin, bout
  Divider #(.width(16)) divider_2 (
    .a(subtractor_1_out), .b(16'h3e8), .out({divider_2_out, out_3}));  // open: upper, rem
  Multiplier #(.width(16)) multiplier_2 (
    .a({divider_2_out, out_3}), .b(16'h3e8), .out(multiplier_2_out));  // open: cin, cout
  Subtractor #(.width(16)) subtractor_2 (
    .a(subtractor_1_out), .b(multiplier_2_out), .out(subtractor_2_out));  // open: bin, bout
  Divider #(.width(16)) divider_3 (.a(subtractor_2_out), .b(16'h64), .out({divider_3_out, out_4}));  // open: upper, rem
  Multiplier #(.width(16)) multiplier_3 (
    .a({divider_3_out, out_4}), .b(16'h64), .out(multiplier_3_out));  // open: cin, cout
  Subtractor #(.width(16)) subtractor_3 (
    .a(subtractor_2_out), .b(multiplier_3_out), .out(subtractor_3_out));  // open: bin, bout
  Divider #(.width(16)) divider_4 (.a(subtractor_3_out), .b(16'ha), .out({divider_4_out, out_5}));  // open: upper, rem
  Multiplier #(.width(16)) multiplier_4 (
    .a({divider_4_out, out_5}), .b(16'ha), .out(multiplier_4_out));  // open: cin, cout
  Subtractor #(.width(16)) subtractor_4 (
    .a(subtractor_3_out), .b(multiplier_4_out), .out(subtractor_4_out));  // open: bin, bout
  Divider #(.width(16)) divider_5 (.a(subtractor_4_out), .b(16'h1), .out({divider_5_out, out_6}));  // open: upper, rem
  Multiplier #(.width(16)) multiplier_5 (
    .a({divider_5_out, out_6}), .b(16'h1), .out(multiplier_5_out));  // open: cin, cout
  Subtractor #(.width(16)) subtractor_5 (.a(subtractor_4_out), .b(multiplier_5_out));  // open: out, bin, bout
endmodule

module keyboard (
  input  in_1,
  input  in_2,
  input  in_3,
  input  in_4,
  input  in_5,
  input  in_6,
  input  in_7,
  input  in_8,
  input  in_9,
  input  in_10,
  input  in_11,
  input  in_12,
  input  in_13,
  input  in_14,
  input  in_15,
  output [2:0] out_16,
  output [7:0] out_17,
  output out_18
);

  wire function_keyboard_1_out_6, numeric_keyboard_1_out_12;

  function_keyboard function_keyboard_1 (
    .a(in_5), .b(in_4), .c(in_3), .d(in_2), .e(in_1), .out_6(function_keyboard_1_out_6), .x(out_16[2]),
    .y(out_16[1]), .z(out_16[0]));
  numeric_keyboard numeric_keyboard_1 (
    .a(in_6), .b(in_7), .c(in_8), .d(in_9), .e(in_10), .f(in_11), .g(in_12), .h(in_13), .x2(in_14),
    .x3(in_15), .out_11(out_17), .out_12(numeric_keyboard_1_out_12));
  or or_1 (out_18, function_keyboard_1_out_6, numeric_keyboard_1_out_12);
endmodule

module CPU (
  input  clk,
  input  [15:0] in_2,
  input  in_3,
  output [15:0] out_4
);

  wire and_1_out, n8_bits_or_1_out_2, not_1_out;
  wire [7:0] register_1_q, register_2_q, register_3_q, register_4_q, register_5_q;
  wire [15:0] adder_1_out, adder_2_out, adder_3_out, adder_4_out, multiplier_1_out, multiplier_2_out,
       multiplier_3_out, multiplier_4_out;

  _8_bits_OR u_8_bits_or_1 (.in_1(in_2[7:0]), .out_2(n8_bits_or_1_out_2));
  not not_1 (not_1_out, n8_bits_or_1_out_2);
  and and_1 (and_1_out, not_1_out, in_3);
  Register #(.trigger("falling")) register_1 (.D(in_2[15:8]), .Q(register_1_q), .clk(and_1_out));  // open: en, clr
  Register register_2 (.D(register_1_q), .Q(register_2_q), .clk(and_1_out));  // open: en, clr
  Register register_3 (.D(register_2_q), .Q(register_3_q), .clk(and_1_out));  // open: en, clr
  Register register_4 (.D(register_3_q), .Q(register_4_q), .clk(and_1_out));  // open: en, clr
  Multiplier #(.width(16)) multiplier_1 (
    .a({{8{1'b0}}, register_5_q}), .b(16'h2710), .out(multiplier_1_out));  // open: cin, cout
  Multiplier #(.width(16)) multiplier_2 (
    .a({{8{1'b0}}, register_4_q}), .b(16'h3e8), .out(multiplier_2_out));  // open: cin, cout
  Multiplier #(.width(16)) multiplier_3 (
    .a({{8{1'b0}}, register_3_q}), .b(16'h64), .out(multiplier_3_out));  // open: cin, cout
  Multiplier #(.width(16)) multiplier_4 (
    .a({{8{1'b0}}, register_2_q}), .b(16'ha), .out(multiplier_4_out));  // open: cin, cout
  Register register_5 (.D(register_4_q), .Q(register_5_q), .clk(and_1_out));  // open: en, clr
  Adder #(.width(16)) adder_1 (.a(multiplier_1_out), .b(multiplier_2_out), .out(adder_1_out));  // open: cin, cout
  Adder #(.width(16)) adder_2 (.a(adder_1_out), .b(multiplier_3_out), .out(adder_2_out));  // open: cin, cout
  Adder #(.width(16)) adder_3 (.a(adder_2_out), .b(multiplier_4_out), .out(adder_3_out));  // open: cin, cout
  Adder #(.width(16)) adder_4 (.a(adder_3_out), .b({{8{1'b0}}, register_1_q}), .out(adder_4_out));  // open: cin, cout
  Register #(.width(16)) register_6 (.D(adder_4_out), .Q(out_4), .clk(clk));  // open: en, clr
endmodule

module bcd_to_16bits (
  input  clk,
  input  [7:0] in_2,
  input  in_3,
  input  in_4,
  output [15:0] out_5
);

  wire [7:0] register_1_q, register_2_q, register_3_q, register_4_q, register_5_q;
  wire [15:0] adder_1_out, adder_2_out, adder_3_out, adder_4_out, multiplier_1_out, multiplier_2_out,
       multiplier_3_out, multiplier_4_out;

  Register register_1 (.D(in_2), .Q(register_1_q), .clk(in_3), .clr(in_4));  // open: en
  Register register_2 (.D(register_1_q), .Q(register_2_q), .clk(in_3), .clr(in_4));  // open: en
  Register register_3 (.D(register_2_q), .Q(register_3_q), .clk(in_3), .clr(in_4));  // open: en
  Register register_4 (.D(register_3_q), .Q(register_4_q), .clk(in_3), .clr(in_4));  // open: en
  Multiplier #(.width(16)) multiplier_1 (
    .a({{8{1'b0}}, register_5_q}), .b(16'h2710), .out(multiplier_1_out));  // open: cin, cout
  Multiplier #(.width(16)) multiplier_2 (
    .a({{8{1'b0}}, register_4_q}), .b(16'h3e8), .out(multiplier_2_out));  // open: cin, cout
  Multiplier #(.width(16)) multiplier_3 (
    .a({{8{1'b0}}, register_3_q}), .b(16'h64), .out(multiplier_3_out));  // open: cin, cout
  Multiplier #(.width(16)) multiplier_4 (
    .a({{8{1'b0}}, register_2_q}), .b(16'ha), .out(multiplier_4_out));  // open: cin, cout
  Register register_5 (.D(register_4_q), .Q(register_5_q), .clk(in_3), .clr(in_4));  // open: en
  Adder #(.width(16)) adder_1 (.a(multiplier_1_out), .b(multiplier_2_out), .out(adder_1_out));  // open: cin, cout
  Adder #(.width(16)) adder_2 (.a(adder_1_out), .b(multiplier_3_out), .out(adder_2_out));  // open: cin, cout
  Adder #(.width(16)) adder_3 (.a(adder_2_out), .b(multiplier_4_out), .out(adder_3_out));  // open: cin, cout
  Adder #(.width(16)) adder_4 (.a(adder_3_out), .b({{8{1'b0}}, register_1_q}), .out(adder_4_out));  // open: cin, cout
  Register #(.width(16)) register_6 (.D(adder_4_out), .Q(out_5), .clk(clk));  // open: en, clr
endmodule

module numeric_keyboard (
  input  a,
  input  b,
  input  c,
  input  d,
  input  e,
  input  f,
  input  g,
  input  h,
  input  x2,
  input  x3,
  output [7:0] out_11,
  output out_12
);

  wire and_1_out, and_2_out, and_3_out, and_4_out, and_5_out, and_6_out, and_7_out, and_8_out, and_9_out,
       and_10_out, and_11_out, and_12_out, and_13_out, and_14_out, and_15_out, not_1_out, not_2_out,
       not_3_out, not_4_out, not_5_out, not_6_out, not_7_out, not_8_out, not_9_out, not_10_out, not_11_out,
       not_12_out, not_13_out, not_14_out, not_15_out, not_16_out, not_17_out, not_18_out, not_19_out,
       not_20_out, not_21_out, not_22_out, not_23_out, not_24_out, not_25_out, not_26_out, not_27_out,
       not_28_out, not_29_out, not_30_out, not_31_out, not_32_out, not_33_out, not_34_out, not_35_out,
       not_36_out, not_37_out, not_38_out, not_39_out, not_40_out, not_41_out, not_42_out, not_43_out,
       not_44_out, not_45_out, not_46_out, not_47_out, not_48_out, not_49_out, not_50_out, not_51_out,
       not_52_out, not_53_out, not_54_out, not_55_out, not_56_out, not_57_out, not_58_out, not_59_out,
       not_60_out, not_61_out, not_62_out, not_63_out, not_64_out, not_65_out, not_66_out, not_67_out,
       not_68_out, not_69_out, not_70_out, not_71_out, not_72_out, not_73_out, not_74_out, not_75_out,
       not_76_out, not_77_out, not_78_out, not_79_out, not_80_out, not_81_out, not_82_out, not_83_out,
       not_84_out, not_85_out, not_86_out, not_87_out, not_88_out, not_89_out;

  not not_1 (not_1_out, c);
  not not_2 (not_2_out, d);
  not not_3 (not_3_out, e);
  not not_4 (not_4_out, f);
  not not_5 (not_5_out, g);
  not not_6 (not_6_out, h);
  not not_7 (not_7_out, x2);
  not not_8 (not_8_out, x3);
  not not_9 (not_9_out, c);
  not not_10 (not_10_out, d);
  not not_11 (not_11_out, e);
  not not_12 (not_12_out, f);
  not not_13 (not_13_out, g);
  not not_14 (not_14_out, h);
  not not_15 (not_15_out, x2);
  not not_16 (not_16_out, x3);
  not not_17 (not_17_out, a);
  not not_18 (not_18_out, b);
  not not_19 (not_19_out, g);
  not not_20 (not_20_out, h);
  not not_21 (not_21_out, x2);
  not not_22 (not_22_out, x3);
  not not_23 (not_23_out, a);
  not not_24 (not_24_out, b);
  not not_25 (not_25_out, g);
  not not_26 (not_26_out, h);
  not not_27 (not_27_out, x2);
  not not_28 (not_28_out, x3);
  not not_29 (not_29_out, a);
  not not_30 (not_30_out, b);
  not not_31 (not_31_out, g);
  not not_32 (not_32_out, h);
  not not_33 (not_33_out, x2);
  not not_34 (not_34_out, x3);
  not not_35 (not_35_out, a);
  not not_36 (not_36_out, b);
  not not_37 (not_37_out, g);
  not not_38 (not_38_out, h);
  not not_39 (not_39_out, x2);
  not not_40 (not_40_out, x3);
  not not_41 (not_41_out, a);
  not not_42 (not_42_out, b);
  not not_43 (not_43_out, e);
  not not_44 (not_44_out, f);
  not not_45 (not_45_out, x2);
  not not_46 (not_46_out, x3);
  not not_47 (not_47_out, a);
  not not_48 (not_48_out, b);
  not not_49 (not_49_out, e);
  not not_50 (not_50_out, f);
  not not_51 (not_51_out, x2);
  not not_52 (not_52_out, x3);
  not not_53 (not_53_out, a);
  not not_54 (not_54_out, b);
  not not_55 (not_55_out, e);
  not not_56 (not_56_out, f);
  not not_57 (not_57_out, x2);
  not not_58 (not_58_out, x3);
  not not_59 (not_59_out, a);
  not not_60 (not_60_out, b);
  not not_61 (not_61_out, e);
  not not_62 (not_62_out, f);
  not not_63 (not_63_out, x2);
  not not_64 (not_64_out, x3);
  not not_65 (not_65_out, b);
  not not_66 (not_66_out, d);
  not not_67 (not_67_out, f);
  not not_68 (not_68_out, h);
  not not_69 (not_69_out, x3);
  not not_70 (not_70_out, b);
  not not_71 (not_71_out, d);
  not not_72 (not_72_out, f);
  not not_73 (not_73_out, h);
  not not_74 (not_74_out, x3);
  not not_75 (not_75_out, b);
  not not_76 (not_76_out, d);
  not not_77 (not_77_out, f);
  not not_78 (not_78_out, h);
  not not_79 (not_79_out, x3);
  not not_80 (not_80_out, b);
  not not_81 (not_81_out, d);
  not not_82 (not_82_out, f);
  not not_83 (not_83_out, h);
  not not_84 (not_84_out, x3);
  not not_85 (not_85_out, b);
  not not_86 (not_86_out, d);
  not not_87 (not_87_out, f);
  not not_88 (not_88_out, h);
  not not_89 (not_89_out, x3);
  and and_1 (and_1_out, b, not_1_out, not_2_out, not_3_out, not_4_out, not_5_out, not_6_out, not_7_out, not_8_out);
  and and_2 (and_2_out, a, not_9_out, not_10_out, not_11_out, not_12_out, not_13_out, not_14_out, not_15_out, not_16_out);
  and and_3 (and_3_out, not_17_out, not_18_out, f, not_19_out, not_20_out, not_21_out, not_22_out);
  and and_4 (and_4_out, not_23_out, not_24_out, e, not_25_out, not_26_out, not_27_out, not_28_out);
  and and_5 (and_5_out, not_29_out, not_30_out, d, not_31_out, not_32_out, not_33_out, not_34_out);
  and and_6 (and_6_out, not_35_out, not_36_out, c, not_37_out, not_38_out, not_39_out, not_40_out);
  and and_7 (and_7_out, not_41_out, not_42_out, not_43_out, not_44_out, h, not_45_out, not_46_out);
  and and_8 (and_8_out, not_47_out, not_48_out, not_49_out, not_50_out, g, not_51_out, not_52_out);
  and and_9 (and_9_out, not_53_out, not_54_out, d, not_55_out, not_56_out, not_57_out, not_58_out);
  and and_10 (and_10_out, not_59_out, not_60_out, c, not_61_out, not_62_out, not_63_out, not_64_out);
  and and_11 (and_11_out, not_65_out, not_66_out, not_67_out, not_68_out, x2, not_69_out);
  and and_12 (and_12_out, not_70_out, not_71_out, not_72_out, g, not_73_out, not_74_out);
  and and_13 (and_13_out, not_75_out, not_76_out, e, not_77_out, not_78_out, not_79_out);
  and and_14 (and_14_out, not_80_out, c, not_81_out, not_82_out, not_83_out, not_84_out);
  and and_15 (and_15_out, a, not_85_out, not_86_out, not_87_out, not_88_out, not_89_out);
  or or_1 (out_12, a, b, c, d, e, f, g, h, x2, x3);
  or or_2 (out_11[3], and_1_out, and_2_out);
  or or_3 (out_11[2], and_3_out, and_4_out, and_5_out, and_6_out);
  or or_4 (out_11[1], and_7_out, and_8_out, and_9_out, and_10_out);
  or or_5 (out_11[0], and_11_out, and_12_out, and_13_out, and_14_out, and_15_out);

  assign out_11[7:4] = 4'b0000;
endmodule

module function_keyboard (
  input  a,
  input  b,
  input  c,
  input  d,
  input  e,
  output out_6,
  output x,
  output y,
  output z
);

  wire and_1_out, and_2_out, and_3_out, and_4_out, and_5_out, and_6_out, and_7_out, not_1_out, not_2_out,
       not_3_out, not_4_out, not_5_out, not_6_out, not_7_out, not_8_out, not_9_out, not_10_out, not_11_out,
       not_12_out, not_13_out, not_14_out, not_15_out, not_16_out, not_17_out, not_18_out, not_19_out,
       not_20_out, not_21_out, not_22_out, not_23_out, not_24_out, not_25_out, not_26_out, not_27_out,
       not_28_out;

  or or_1 (out_6, a, b, c, d, e);
  not not_1 (not_1_out, a);
  not not_2 (not_2_out, c);
  not not_3 (not_3_out, d);
  not not_4 (not_4_out, e);
  not not_5 (not_5_out, b);
  not not_6 (not_6_out, c);
  not not_7 (not_7_out, d);
  not not_8 (not_8_out, e);
  not not_9 (not_9_out, a);
  not not_10 (not_10_out, b);
  not not_11 (not_11_out, c);
  not not_12 (not_12_out, e);
  not not_13 (not_13_out, a);
  not not_14 (not_14_out, b);
  not not_15 (not_15_out, d);
  not not_16 (not_16_out, e);
  not not_17 (not_17_out, a);
  not not_18 (not_18_out, b);
  not not_19 (not_19_out, c);
  not not_20 (not_20_out, d);
  not not_21 (not_21_out, a);
  not not_22 (not_22_out, b);
  not not_23 (not_23_out, d);
  not not_24 (not_24_out, e);
  not not_25 (not_25_out, b);
  not not_26 (not_26_out, c);
  not not_27 (not_27_out, d);
  not not_28 (not_28_out, e);
  and and_1 (and_1_out, not_1_out, b, not_2_out, not_3_out, not_4_out);
  and and_2 (and_2_out, a, not_5_out, not_6_out, not_7_out, not_8_out);
  and and_3 (and_3_out, not_9_out, not_10_out, not_11_out, d, not_12_out);
  and and_4 (and_4_out, not_13_out, not_14_out, c, not_15_out, not_16_out);
  and and_5 (and_5_out, not_17_out, not_18_out, not_19_out, not_20_out, e);
  and and_6 (and_6_out, not_21_out, not_22_out, c, not_23_out, not_24_out);
  and and_7 (and_7_out, a, not_25_out, not_26_out, not_27_out, not_28_out);
  or or_2 (x, and_1_out, and_2_out);
  or or_3 (y, and_3_out, and_4_out);
  or or_4 (z, and_5_out, and_6_out, and_7_out);
endmodule

module keyboard_v2 (
  input  in_1,
  input  in_2,
  input  in_3,
  input  in_4,
  input  in_5,
  input  in_6,
  input  in_7,
  input  in_8,
  input  in_9,
  input  in_10,
  input  in_11,
  input  in_12,
  input  in_13,
  input  in_14,
  input  in_15,
  input  in_16,
  output [15:0] out_17,
  output out_18
);

  wire or_1_out, or_2_out;

  or or_1 (or_1_out, in_6, in_5, in_4, in_3, in_2, in_1);
  function_keyboard_v2 function_keyboard_v2_1 (
    .a(in_6), .b(in_5), .c(in_4), .d(in_3), .e(in_2), .f(in_1), .out_7(out_17[7:0]));
  numeric_keyboard_v2 numeric_keyboard_v2_1 (
    .a(in_7), .b(in_8), .c(in_9), .d(in_10), .e(in_11), .f(in_12), .g(in_13), .h(in_14), .x2(in_15),
    .x3(in_16), .out_11(out_17[15:8]));
  or or_2 (or_2_out, in_16, in_15, in_14, in_13, in_12, in_11, in_10, in_9, in_8, in_7);
  or or_3 (out_18, or_2_out, or_1_out);
endmodule

module _8_bits_OR (
  input  [7:0] in_1,
  output out_2
);

  or or_1 (out_2, in_1[0], in_1[1], in_1[2], in_1[3], in_1[4], in_1[5], in_1[6], in_1[7]);
endmodule

module function_keyboard_v2 (
  input  a,
  input  b,
  input  c,
  input  d,
  input  e,
  input  f,
  output [7:0] out_7
);

  wire and_1_out, and_2_out, and_3_out, and_4_out, and_5_out, and_6_out, and_7_out, and_8_out, and_9_out,
       not_1_out, not_2_out, not_3_out, not_4_out, not_5_out, not_6_out, not_7_out, not_8_out, not_9_out,
       not_10_out, not_11_out, not_12_out, not_13_out, not_14_out, not_15_out, not_16_out, not_17_out,
       not_18_out, not_19_out, not_20_out, not_21_out, not_22_out, not_23_out, not_24_out, not_25_out,
       not_26_out, not_27_out, not_28_out, not_29_out, not_30_out, not_31_out, not_32_out, not_33_out,
       not_34_out, not_35_out, not_36_out, not_37_out, not_38_out, not_39_out, not_40_out, not_41_out,
       not_42_out, not_43_out, not_44_out, not_45_out;

  not not_1 (not_1_out, a);
  not not_2 (not_2_out, b);
  not not_3 (not_3_out, d);
  not not_4 (not_4_out, e);
  not not_5 (not_5_out, f);
  not not_6 (not_6_out, a);
  not not_7 (not_7_out, c);
  not not_8 (not_8_out, d);
  not not_9 (not_9_out, e);
  not not_10 (not_10_out, f);
  not not_11 (not_11_out, b);
  not not_12 (not_12_out, c);
  not not_13 (not_13_out, d);
  not not_14 (not_14_out, e);
  not not_15 (not_15_out, f);
  not not_16 (not_16_out, a);
  not not_17 (not_17_out, b);
  not not_18 (not_18_out, c);
  not not_19 (not_19_out, d);
  not not_20 (not_20_out, f);
  not not_21 (not_21_out, a);
  not not_22 (not_22_out, b);
  not not_23 (not_23_out, c);
  not not_24 (not_24_out, e);
  not not_25 (not_25_out, f);
  not not_26 (not_26_out, b);
  not not_27 (not_27_out, c);
  not not_28 (not_28_out, d);
  not not_29 (not_29_out, e);
  not not_30 (not_30_out, f);
  not not_31 (not_31_out, a);
  not not_32 (not_32_out, b);
  not not_33 (not_33_out, c);
  not not_34 (not_34_out, d);
  not not_35 (not_35_out, e);
  not not_36 (not_36_out, a);
  not not_37 (not_37_out, b);
  not not_38 (not_38_out, c);
  not not_39 (not_39_out, e);
  not not_40 (not_40_out, f);
  not not_41 (not_41_out, a);
  not not_42 (not_42_out, c);
  not not_43 (not_43_out, d);
  not not_44 (not_44_out, e);
  not not_45 (not_45_out, f);
  and and_1 (and_1_out, not_1_out, not_2_out, c, not_3_out, not_4_out, not_5_out);
  and and_2 (and_2_out, not_6_out, b, not_7_out, not_8_out, not_9_out, not_10_out);
  and and_3 (and_3_out, a, not_11_out, not_12_out, not_13_out, not_14_out, not_15_out);
  and and_4 (and_4_out, not_16_out, not_17_out, not_18_out, not_19_out, e, not_20_out);
  and and_5 (and_5_out, not_21_out, not_22_out, not_23_out, d, not_24_out, not_25_out);
  and and_6 (and_6_out, a, not_26_out, not_27_out, not_28_out, not_29_out, not_30_out);
  and and_7 (and_7_out, not_31_out, not_32_out, not_33_out, not_34_out, not_35_out, f);
  and and_8 (and_8_out, not_36_out, not_37_out, not_38_out, d, not_39_out, not_40_out);
  and and_9 (and_9_out, not_41_out, b, not_42_out, not_43_out, not_44_out, not_45_out);
  or or_1 (out_7[2], and_1_out, and_2_out, and_3_out);
  or or_2 (out_7[1], and_4_out, and_5_out, and_6_out);
  or or_3 (out_7[0], and_7_out, and_8_out, and_9_out);

  assign out_7[7:3] = {5{1'b0}};
endmodule

module numeric_keyboard_v2 (
  input  a,
  input  b,
  input  c,
  input  d,
  input  e,
  input  f,
  input  g,
  input  h,
  input  x2,
  input  x3,
  output [7:0] out_11
);

  wire and_1_out, and_2_out, and_3_out, and_4_out, and_5_out, and_6_out, and_7_out, and_8_out, and_9_out,
       and_10_out, and_11_out, and_12_out, and_13_out, and_14_out, and_15_out, not_1_out, not_2_out,
       not_3_out, not_4_out, not_5_out, not_6_out, not_7_out, not_8_out, not_9_out, not_10_out, not_11_out,
       not_12_out, not_13_out, not_14_out, not_15_out, not_16_out, not_17_out, not_18_out, not_19_out,
       not_20_out, not_21_out, not_22_out, not_23_out, not_24_out, not_25_out, not_26_out, not_27_out,
       not_28_out, not_29_out, not_30_out, not_31_out, not_32_out, not_33_out, not_34_out, not_35_out,
       not_36_out, not_37_out, not_38_out, not_39_out, not_40_out, not_41_out, not_42_out, not_43_out,
       not_44_out, not_45_out, not_46_out, not_47_out, not_48_out, not_49_out, not_50_out, not_51_out,
       not_52_out, not_53_out, not_54_out, not_55_out, not_56_out, not_57_out, not_58_out, not_59_out,
       not_60_out, not_61_out, not_62_out, not_63_out, not_64_out, not_65_out, not_66_out, not_67_out,
       not_68_out, not_69_out, not_70_out, not_71_out, not_72_out, not_73_out, not_74_out, not_75_out,
       not_76_out, not_77_out, not_78_out, not_79_out, not_80_out, not_81_out, not_82_out, not_83_out,
       not_84_out, not_85_out, not_86_out, not_87_out, not_88_out, not_89_out;

  not not_1 (not_1_out, c);
  not not_2 (not_2_out, d);
  not not_3 (not_3_out, e);
  not not_4 (not_4_out, f);
  not not_5 (not_5_out, g);
  not not_6 (not_6_out, h);
  not not_7 (not_7_out, x2);
  not not_8 (not_8_out, x3);
  not not_9 (not_9_out, c);
  not not_10 (not_10_out, d);
  not not_11 (not_11_out, e);
  not not_12 (not_12_out, f);
  not not_13 (not_13_out, g);
  not not_14 (not_14_out, h);
  not not_15 (not_15_out, x2);
  not not_16 (not_16_out, x3);
  not not_17 (not_17_out, a);
  not not_18 (not_18_out, b);
  not not_19 (not_19_out, g);
  not not_20 (not_20_out, h);
  not not_21 (not_21_out, x2);
  not not_22 (not_22_out, x3);
  not not_23 (not_23_out, a);
  not not_24 (not_24_out, b);
  not not_25 (not_25_out, g);
  not not_26 (not_26_out, h);
  not not_27 (not_27_out, x2);
  not not_28 (not_28_out, x3);
  not not_29 (not_29_out, a);
  not not_30 (not_30_out, b);
  not not_31 (not_31_out, g);
  not not_32 (not_32_out, h);
  not not_33 (not_33_out, x2);
  not not_34 (not_34_out, x3);
  not not_35 (not_35_out, a);
  not not_36 (not_36_out, b);
  not not_37 (not_37_out, g);
  not not_38 (not_38_out, h);
  not not_39 (not_39_out, x2);
  not not_40 (not_40_out, x3);
  not not_41 (not_41_out, a);
  not not_42 (not_42_out, b);
  not not_43 (not_43_out, e);
  not not_44 (not_44_out, f);
  not not_45 (not_45_out, x2);
  not not_46 (not_46_out, x3);
  not not_47 (not_47_out, a);
  not not_48 (not_48_out, b);
  not not_49 (not_49_out, e);
  not not_50 (not_50_out, f);
  not not_51 (not_51_out, x2);
  not not_52 (not_52_out, x3);
  not not_53 (not_53_out, a);
  not not_54 (not_54_out, b);
  not not_55 (not_55_out, e);
  not not_56 (not_56_out, f);
  not not_57 (not_57_out, x2);
  not not_58 (not_58_out, x3);
  not not_59 (not_59_out, a);
  not not_60 (not_60_out, b);
  not not_61 (not_61_out, e);
  not not_62 (not_62_out, f);
  not not_63 (not_63_out, x2);
  not not_64 (not_64_out, x3);
  not not_65 (not_65_out, b);
  not not_66 (not_66_out, d);
  not not_67 (not_67_out, f);
  not not_68 (not_68_out, h);
  not not_69 (not_69_out, x3);
  not not_70 (not_70_out, b);
  not not_71 (not_71_out, d);
  not not_72 (not_72_out, f);
  not not_73 (not_73_out, h);
  not not_74 (not_74_out, x3);
  not not_75 (not_75_out, b);
  not not_76 (not_76_out, d);
  not not_77 (not_77_out, f);
  not not_78 (not_78_out, h);
  not not_79 (not_79_out, x3);
  not not_80 (not_80_out, b);
  not not_81 (not_81_out, d);
  not not_82 (not_82_out, f);
  not not_83 (not_83_out, h);
  not not_84 (not_84_out, x3);
  not not_85 (not_85_out, b);
  not not_86 (not_86_out, d);
  not not_87 (not_87_out, f);
  not not_88 (not_88_out, h);
  not not_89 (not_89_out, x3);
  and and_1 (and_1_out, b, not_1_out, not_2_out, not_3_out, not_4_out, not_5_out, not_6_out, not_7_out, not_8_out);
  and and_2 (and_2_out, a, not_9_out, not_10_out, not_11_out, not_12_out, not_13_out, not_14_out, not_15_out, not_16_out);
  and and_3 (and_3_out, not_17_out, not_18_out, f, not_19_out, not_20_out, not_21_out, not_22_out);
  and and_4 (and_4_out, not_23_out, not_24_out, e, not_25_out, not_26_out, not_27_out, not_28_out);
  and and_5 (and_5_out, not_29_out, not_30_out, d, not_31_out, not_32_out, not_33_out, not_34_out);
  and and_6 (and_6_out, not_35_out, not_36_out, c, not_37_out, not_38_out, not_39_out, not_40_out);
  and and_7 (and_7_out, not_41_out, not_42_out, not_43_out, not_44_out, h, not_45_out, not_46_out);
  and and_8 (and_8_out, not_47_out, not_48_out, not_49_out, not_50_out, g, not_51_out, not_52_out);
  and and_9 (and_9_out, not_53_out, not_54_out, d, not_55_out, not_56_out, not_57_out, not_58_out);
  and and_10 (and_10_out, not_59_out, not_60_out, c, not_61_out, not_62_out, not_63_out, not_64_out);
  and and_11 (and_11_out, not_65_out, not_66_out, not_67_out, not_68_out, x2, not_69_out);
  and and_12 (and_12_out, not_70_out, not_71_out, not_72_out, g, not_73_out, not_74_out);
  and and_13 (and_13_out, not_75_out, not_76_out, e, not_77_out, not_78_out, not_79_out);
  and and_14 (and_14_out, not_80_out, c, not_81_out, not_82_out, not_83_out, not_84_out);
  and and_15 (and_15_out, a, not_85_out, not_86_out, not_87_out, not_88_out, not_89_out);
  or or_1 (out_11[3], and_1_out, and_2_out);
  or or_2 (out_11[2], and_3_out, and_4_out, and_5_out, and_6_out);
  or or_3 (out_11[1], and_7_out, and_8_out, and_9_out, and_10_out);
  or or_4 (out_11[0], and_11_out, and_12_out, and_13_out, and_14_out, and_15_out);

  assign out_11[7:4] = 4'b0000;
endmodule

module Test_circuit (
  output [15:0] out_1,
  output [15:0] out_2
);

  wire _0_out, _1_out, _2_out, _3_out, _4_out, _5_out, _6_out, _7_out, _8_out, _9_out, button_2_out,
       button_3_out, button_4_out, button_5_out, button_out, C_out, clock_1_out, keyboard_v2_1_out_18;

  Button _8 (.out(_8_out));
  Button _7 (.out(_7_out));
  Button _5 (.out(_5_out));
  Button _4 (.out(_4_out));
  Button _2 (.out(_2_out));
  Button _1 (.out(_1_out));
  Button _0 (.out(_0_out));
  Button _9 (.out(_9_out));
  Button C (.out(C_out));
  Button button (.out(button_out));
  Button _6 (.out(_6_out));
  Button button_2 (.out(button_2_out));
  Button _3 (.out(_3_out));
  Button button_3 (.out(button_3_out));
  Button button_4 (.out(button_4_out));
  Button button_5 (.out(button_5_out));
  keyboard_v2 keyboard_v2_1 (
    .in_7(_9_out), .in_8(_8_out), .in_9(_7_out), .in_10(_6_out), .in_11(_5_out), .in_12(_4_out),
    .in_13(_3_out), .in_14(_2_out), .in_15(_1_out), .in_16(_0_out), .out_17(out_2), .in_1(button_5_out),
    .in_2(button_4_out), .in_3(button_3_out), .in_4(button_2_out), .in_5(button_out), .in_6(C_out),
    .out_18(keyboard_v2_1_out_18));
  Clock clock_1 (.out(clock_1_out));
  CPU cpu_1 (.clk(clock_1_out), .in_2(out_2), .in_3(keyboard_v2_1_out_18), .out_4(out_1));
endmodule

module _9_bits_circuit (
  input  [7:0] in_1,
  input  in_2,
  output out_3
);

  or or_1 (out_3, in_1[0], in_1[1], in_1[2], in_1[3], in_1[4], in_1[5], in_1[6], in_1[7], in_2);
endmodule
